// Logisim project riscv.circ as structural Verilog: 8 circuits, main circuit RISCV32
module RISCV32 (
);

  wire AUIPC_q, bypass_black_box_1_p3, clk, comparator_black_box_1_p4, DE_EX_JAL_q, DE_EX_JALR_q, DE_EX_LB_q,
       DE_EX_LW_q, DE_EX_regWE_q, DE_EX_SB_q, DE_EX_set_q, DE_EX_shiftreg_q, DE_EX_SW_q, DE_EX_SWSTALL_q,
       DE_EX_useImm_q, decode_1_auipc, decode_1_jal, decode_1_jalr, decode_1_lb, decode_1_lw, decode_1_regwe,
       decode_1_sb, decode_1_set, decode_1_setsign, decode_1_shiftbyregval, decode_1_sw, decode_1_useimm,
       decode_1_zeroouta, EX_M_LB_q, EX_M_LW_q, EX_M_SB_q, EX_M_SW_q, EX_M_SWSTALL_q, execute_1_branch,
       M_W_LB_q, M_W_LW_q, not_1_out, or_1_out, or_4_out, or_5_out, or_6_out, register_2_q,
       registerfile_1_p3, set_signed_q, stalllogic_1_stall, xor_1_out, xor_2_out, ZapIF_q;
  wire [1:0] bypass_black_box_1_p7, bypass_black_box_1_p8;
  wire [3:0] DE_EX_ALUop_q, decode_1_aluop, multiplexer_9_out, or_2_out;
  wire [3:3] or_3_out;
  wire [4:0] bypass_black_box_1_p4, DE_EX_rd_q, decode_1_rd, decode_1_rs1, decode_1_rs2, registerfile_1_p4,
       rs1_q, rs2_q;
  wire [5:0] DE_EX_BranchBits_q, decode_1_branchbits;
  wire [31:0] bit_extender_1_out, DE_EX_A_q, DE_EX_B_q, DE_EX_BranchImm_q, DE_EX_imm_q, DE_EX_JALIMM_q,
       DE_EX_PC_q, DE_EX_PCplus4_q, DE_EX_StoreImm_q, decode_1_branchimm, decode_1_imm, decode_1_jalimm,
       decode_1_storeimm, EX_M_B_q, EX_M_Result_q, execute_1_result, IF_DE_instr_q, IF_DE_PCplusFOUR_q,
       increment_pc_1_out_2, M_W_Data_q, M_W_Result_q, multiplexer_1_out, multiplexer_2_out,
       multiplexer_3_out, multiplexer_4_out, multiplexer_5_out, multiplexer_6_out, multiplexer_7_out,
       multiplexer_8_out, mux3to1_1_out_5, mux3to1_2_out_5, PC_q, ram_1_p7, register_1_q, registerfile_1_p1,
       registerfile_1_p7, registerfile_1_p8, risc_vprogramrom_1_p2;

  Clock clock_1 (.out(clk));
  Register #(.width(32)) register_1 (.D(multiplexer_1_out), .clk(clk), .Q(register_1_q));  // open: en, clr
  Multiplexer #(.width(32), .enable("false")) multiplexer_1 (
    .in0(multiplexer_2_out), .in1(PC_q), .out(multiplexer_1_out), .sel(stalllogic_1_stall));
  Multiplexer #(.width(32), .enable("false")) multiplexer_2 (
    .in0(increment_pc_1_out_2), .in1(execute_1_result), .out(multiplexer_2_out), .sel(or_1_out));
  or or_1 (or_1_out, DE_EX_JAL_q, DE_EX_JALR_q, execute_1_branch);
  Increment_PC increment_pc_1 (.in_1(register_1_q), .out_2(increment_pc_1_out_2));
  Register #(.width(32)) IF_DE_instr (.D(risc_vprogramrom_1_p2), .clk(clk), .Q(IF_DE_instr_q));  // open: en, clr
  // RISC_VProgramROM risc_vprogramrom_1: pin names not known; wires that end beside it: register_1_q, risc_vprogramrom_1_p2
  Register #(.width(32)) PC (.D(register_1_q), .clk(clk), .Q(PC_q));  // open: en, clr
  Register #(.width(32)) IF_DE_PCplusFOUR (
    .D(increment_pc_1_out_2), .clk(clk), .Q(IF_DE_PCplusFOUR_q));  // open: en, clr
  Register #(.width(1)) ZapIF (.D(or_1_out), .clk(clk), .Q(ZapIF_q));  // open: en, clr
  not not_1 (not_1_out, clk);
  Decode decode_1 (
    .instr(IF_DE_instr_q), .ZapIF(ZapIF_q), .ZapDec(or_1_out), .rs1(decode_1_rs1), .rs2(decode_1_rs2),
    .rd(decode_1_rd), .imm(decode_1_imm), .useImm(decode_1_useimm), .ALUop(decode_1_aluop),
    .regWE(decode_1_regwe), .set(decode_1_set), .shiftbyregval(decode_1_shiftbyregval),
    .setsign(decode_1_setsign), .AUIPC(decode_1_auipc), .ZeroOutA(decode_1_zeroouta), .LW(decode_1_lw),
    .LB(decode_1_lb), .SW(decode_1_sw), .SB(decode_1_sb), .JALimm(decode_1_jalimm), .JAL(decode_1_jal),
    .JALR(decode_1_jalr), .BranchImm(decode_1_branchimm), .BranchBits(decode_1_branchbits),
    .StoreImm(decode_1_storeimm));
  StallLogic stalllogic_1 (
    .LW(DE_EX_LW_q), .LB(DE_EX_LB_q), .IF_D_R1(decode_1_rs1), .D_EX_RD(DE_EX_rd_q), .IF_D_R2(decode_1_rs2),
    .Stall(stalllogic_1_stall));
  // RegisterFile registerfile_1: pin names not known; wires that end beside it: registerfile_1_p1, not_1_out, registerfile_1_p3, registerfile_1_p4, decode_1_rs1, decode_1_rs2, registerfile_1_p7, registerfile_1_p8
  xor xor_1 (xor_1_out, decode_1_regwe, stalllogic_1_stall);
  Register #(.width(1)) register_2 (.D(decode_1_zeroouta), .clk(clk), .Q(register_2_q));  // open: en, clr
  Register #(.width(32)) DE_EX_A (.D(registerfile_1_p7), .clk(clk), .Q(DE_EX_A_q));  // open: en, clr
  Register #(.width(32)) DE_EX_B (.D(registerfile_1_p8), .clk(clk), .Q(DE_EX_B_q));  // open: en, clr
  Register #(.width(5)) rs1 (.D(decode_1_rs1), .clk(clk), .Q(rs1_q));  // open: en, clr
  Register #(.width(5)) rs2 (.D(decode_1_rs2), .clk(clk), .Q(rs2_q));  // open: en, clr
  Register #(.width(5)) DE_EX_rd (.D(decode_1_rd), .clk(clk), .Q(DE_EX_rd_q));  // open: en, clr
  Register #(.width(32)) DE_EX_imm (.D(decode_1_imm), .clk(clk), .Q(DE_EX_imm_q));  // open: en, clr
  Register #(.width(1)) DE_EX_useImm (.D(decode_1_useimm), .clk(clk), .Q(DE_EX_useImm_q));  // open: en, clr
  Register #(.width(4)) DE_EX_ALUop (.D(decode_1_aluop), .clk(clk), .Q(DE_EX_ALUop_q));  // open: en, clr
  Register #(.width(1)) DE_EX_regWE (.D(xor_1_out), .clk(clk), .Q(DE_EX_regWE_q));  // open: en, clr
  Register #(.width(1)) DE_EX_set (.D(decode_1_set), .clk(clk), .Q(DE_EX_set_q));  // open: en, clr
  Register #(.width(1)) DE_EX_shiftreg (.D(decode_1_shiftbyregval), .clk(clk), .Q(DE_EX_shiftreg_q));  // open: en, clr
  Register #(.width(1)) set_signed (.D(decode_1_setsign), .clk(clk), .Q(set_signed_q));  // open: en, clr
  Register #(.width(32)) DE_EX_PC (.D(PC_q), .clk(clk), .Q(DE_EX_PC_q));  // open: en, clr
  Register #(.width(1)) AUIPC (.D(decode_1_auipc), .clk(clk), .Q(AUIPC_q));  // open: en, clr
  Register #(.width(1)) DE_EX_LW (.D(decode_1_lw), .clk(clk), .Q(DE_EX_LW_q));  // open: en, clr
  Register #(.width(1)) DE_EX_LB (.D(decode_1_lb), .clk(clk), .Q(DE_EX_LB_q));  // open: en, clr
  Register #(.width(1)) DE_EX_SW (.D(decode_1_sw), .clk(clk), .Q(DE_EX_SW_q));  // open: en, clr
  Register #(.width(1)) DE_EX_SB (.D(decode_1_sb), .clk(clk), .Q(DE_EX_SB_q));  // open: en, clr
  Register #(.width(1)) DE_EX_SWSTALL (.D(stalllogic_1_stall), .clk(clk), .Q(DE_EX_SWSTALL_q));  // open: en, clr
  Register #(.width(32)) DE_EX_PCplus4 (.D(IF_DE_PCplusFOUR_q), .clk(clk), .Q(DE_EX_PCplus4_q));  // open: en, clr
  Register #(.width(1)) DE_EX_JAL (.D(decode_1_jal), .clk(clk), .Q(DE_EX_JAL_q));  // open: en, clr
  Register #(.width(32)) DE_EX_JALIMM (.D(decode_1_jalimm), .clk(clk), .Q(DE_EX_JALIMM_q));  // open: en, clr
  Register #(.width(1)) DE_EX_JALR (.D(decode_1_jalr), .clk(clk), .Q(DE_EX_JALR_q));  // open: en, clr
  Register #(.width(6)) DE_EX_BranchBits (.D(decode_1_branchbits), .clk(clk), .Q(DE_EX_BranchBits_q));  // open: en, clr
  Register #(.width(32)) DE_EX_BranchImm (.D(decode_1_branchimm), .clk(clk), .Q(DE_EX_BranchImm_q));  // open: en, clr
  Register #(.width(32)) DE_EX_StoreImm (.D(decode_1_storeimm), .clk(clk), .Q(DE_EX_StoreImm_q));  // open: en, clr
  // Bypass_Black_Box bypass_black_box_1: pin names not known; wires that end beside it: rs1_q, rs2_q, bypass_black_box_1_p3, bypass_black_box_1_p4, registerfile_1_p3, registerfile_1_p4, bypass_black_box_1_p7, bypass_black_box_1_p8
  Multiplexer #(.width(32), .enable("false")) multiplexer_3 (
    .in0(DE_EX_imm_q), .in1(DE_EX_JALIMM_q), .out(multiplexer_3_out), .sel(DE_EX_JAL_q));
  MUX3to1 mux3to1_1 (
    .EX(DE_EX_A_q), .out_5(mux3to1_1_out_5), .WB(registerfile_1_p1), .ME(EX_M_Result_q),
    .Sel(bypass_black_box_1_p7));
  MUX3to1 mux3to1_2 (
    .EX(DE_EX_B_q), .out_5(mux3to1_2_out_5), .WB(registerfile_1_p1), .ME(EX_M_Result_q),
    .Sel(bypass_black_box_1_p8));
  Multiplexer #(.width(32), .enable("false")) multiplexer_4 (
    .in0(multiplexer_3_out), .in1(DE_EX_StoreImm_q), .out(multiplexer_4_out), .sel(DE_EX_SW_q));
  Multiplexer #(.width(32), .enable("false")) multiplexer_5 (
    .in0(mux3to1_1_out_5), .in1(DE_EX_PC_q), .out(multiplexer_5_out), .sel(DE_EX_JAL_q));
  Multiplexer #(.width(32), .enable("false")) multiplexer_6 (
    .in0(mux3to1_2_out_5), .in1(DE_EX_imm_q), .out(multiplexer_6_out), .sel(DE_EX_useImm_q));
  // Comparator_Black_Box comparator_black_box_1: pin names not known; wires that end beside it: mux3to1_1_out_5, multiplexer_6_out, set_signed_q, comparator_black_box_1_p4
  assign bit_extender_1_out = {{31{1'b0}}, comparator_black_box_1_p4};  // Bit_Extender bit_extender_1
  // Probe on execute_1_branch
  Execute execute_1 (
    .A(multiplexer_5_out), .B(mux3to1_2_out_5), .rB(rs2_q), .imm(multiplexer_4_out), .useImm(DE_EX_useImm_q),
    .ALUop(DE_EX_ALUop_q), .shiftbyregval(DE_EX_shiftreg_q), .UsePC(AUIPC_q), .PC(DE_EX_PC_q),
    .BranchImm(DE_EX_BranchImm_q), .BranchBits(DE_EX_BranchBits_q), .ZeroA(register_2_q),
    .result(execute_1_result), .Branch(execute_1_branch));
  Multiplexer #(.width(32), .enable("false")) multiplexer_7 (
    .in0(execute_1_result), .in1(bit_extender_1_out), .out(multiplexer_7_out), .sel(DE_EX_set_q));
  Multiplexer #(.width(32), .enable("false")) multiplexer_8 (
    .in0(multiplexer_7_out), .in1(DE_EX_PCplus4_q), .out(multiplexer_8_out), .sel(DE_EX_JAL_q));
  Register #(.width(32)) EX_M_Result (.D(multiplexer_8_out), .clk(clk), .Q(EX_M_Result_q));  // open: en, clr
  Register #(.width(5)) EX_M_rd (.D(DE_EX_rd_q), .clk(clk), .Q(bypass_black_box_1_p4));  // open: en, clr
  Register #(.width(1)) EX_M_regWE (.D(DE_EX_regWE_q), .clk(clk), .Q(bypass_black_box_1_p3));  // open: en, clr
  Register #(.width(1)) EX_M_LW (.D(DE_EX_LW_q), .clk(clk), .Q(EX_M_LW_q));  // open: en, clr
  Register #(.width(1)) EX_M_LB (.D(DE_EX_LB_q), .clk(clk), .Q(EX_M_LB_q));  // open: en, clr
  Register #(.width(1)) EX_M_SW (.D(DE_EX_SW_q), .clk(clk), .Q(EX_M_SW_q));  // open: en, clr
  Register #(.width(1)) EX_M_SB (.D(DE_EX_SB_q), .clk(clk), .Q(EX_M_SB_q));  // open: en, clr
  Register #(.width(32)) EX_M_B (.D(mux3to1_2_out_5), .clk(clk), .Q(EX_M_B_q));  // open: en, clr
  Register #(.width(1)) EX_M_SWSTALL (.D(DE_EX_SWSTALL_q), .clk(clk), .Q(EX_M_SWSTALL_q));  // open: en, clr
  not not_2 (or_2_out[3], or_2_out[0]);
  or or_2 (or_2_out[0], EX_M_LB_q, EX_M_SB_q);
  or or_3 (or_3_out[3], EX_M_LW_q, EX_M_SW_q);
  or or_4 (or_4_out, EX_M_SW_q, EX_M_SB_q);
  Multiplexer #(.width(4), .enable("false")) multiplexer_9 (
    .in0({4{or_3_out[3]}}), .in1({{3{or_2_out[3]}}, or_2_out[0]}), .out(multiplexer_9_out), .sel(or_2_out[0]));
  or or_5 (or_5_out, EX_M_LW_q, EX_M_LB_q);
  xor xor_2 (xor_2_out, or_4_out, EX_M_SWSTALL_q);
  // RAM ram_1: pin names not known; wires that end beside it: EX_M_Result_q[19:0], EX_M_B_q, xor_2_out, multiplexer_9_out, clk, or_5_out, ram_1_p7
  Register #(.width(32)) M_W_Result (.D(EX_M_Result_q), .clk(clk), .Q(M_W_Result_q));  // open: en, clr
  Register #(.width(32)) M_W_Data (.D(ram_1_p7), .clk(clk), .Q(M_W_Data_q));  // open: en, clr
  Register #(.width(1)) M_W_regWE (.D(bypass_black_box_1_p3), .clk(clk), .Q(registerfile_1_p3));  // open: en, clr
  Register #(.width(5)) M_W_rd (.D(bypass_black_box_1_p4), .clk(clk), .Q(registerfile_1_p4));  // open: en, clr
  Register #(.width(1)) M_W_LW (.D(EX_M_LW_q), .clk(clk), .Q(M_W_LW_q));  // open: en, clr
  Register #(.width(1)) M_W_LB (.D(EX_M_LB_q), .clk(clk), .Q(M_W_LB_q));  // open: en, clr
  Multiplexer #(.width(32), .enable("false")) multiplexer_10 (
    .in0(M_W_Result_q), .in1(M_W_Data_q), .out(registerfile_1_p1), .sel(or_6_out));
  or or_6 (or_6_out, M_W_LW_q, M_W_LB_q);

  // Notes on the sheet:
  //   Notes:
  //   not to force you into using a template
  //   This is a working circuit for all of the table A instructions
  //   - Feel free to change the structure of this for any reason
  //   as it is to save you from repeating work you've done,
  //   - Behavior for table B instructions is undefined in this release circuit
  //   - This should pass the sanity check if you submit it as is
  //   Target vs. PC + 4
  //   Target
  //   contents of risc_vprogramrom_1 (hex, n*v repeats v):
  //   addi fp, x0, 0 addi a2, x0, 6 jal ra, m_fibonacci jal x0, exit  m_fibonacci:  addi sp, sp, -32 sw
  //   a2, 28(sp) #n sw a3, 24(sp)  sw a4, 20(sp) #size sw s1, 16(sp) sw s2, 12(sp) sw s3, 8(sp) sw ra,
  //   4(sp) sw fp, 0(sp)   addi fp, sp, 36  bge a2, a4, L0 slli s3, a2, 2  add s3, a3, s3  lw t2, 0(s3)
  //   beq t2, x0, L0 add a0, x0, t2 jal x0, exit_fib  L0: bne a2, x0, L1  jal x0, exit_fib  L1: addi t0,
  //   x0, 1 bne a2,t0, L2 jal x0, exit_fib  L2: addi s1, a2, 0  addi a2, a2, -2 jal ra, m_fibonacci addi
  //   s2, a2, 0  addi a2, s1, -1  jal ra, m_fibonacci add a2, a2, s2 addi a0, a2, 0  bge s1, a4, exit_fib
  //   sw a2, 0(s3)  exit_fib:   lw a3, 24(sp)  lw a4, 20(sp) #size lw s1, 16(sp) lw s2, 12(sp) lw s3,
  //   8(sp) lw ra, 4(sp) lw fp, 0(sp)   addi sp, sp, 32  jalr x0, ra, 0  addi sp, x0, 1024 exit:
  //   Register Write Enable
  //   Okay to leave
  //   these outputs unused
  //   passes with the release circuit
  //   RAM is only here so that the autograder lite
endmodule

module Fetching (
  input  clk,
  output [31:0] intr
);

  wire [31:0] increment_pc_1_out_2, register_1_q;

  Register #(.width(32), .trigger("falling")) register_1 (
    .D(increment_pc_1_out_2), .clk(clk), .Q(register_1_q));  // open: en, clr
  Increment_PC increment_pc_1 (.in_1(register_1_q), .out_2(increment_pc_1_out_2));
endmodule

module Increment_PC (
  input  [31:0] in_1,
  output [31:0] out_2
);

  // Incrementer #(.width(30)) incrementer_1: pin names not known; wires that end beside it: in_1[31:2], out_2[31:2]

  assign out_2[1:0] = in_1[1:0];
endmodule

module Decode (
  input  [31:0] instr,
  input  ZapIF,
  input  ZapDec,
  output [4:0] rs1,
  output [4:0] rs2,
  output [4:0] rd,
  output [31:0] imm,
  output useImm,
  output [3:0] ALUop,
  output regWE,
  output set,
  output shiftbyregval,
  output setsign,
  output AUIPC,
  output ZeroOutA,
  output LW,
  output LB,
  output SW,
  output SB,
  output [31:0] JALimm,
  output JAL,
  output JALR,
  output [31:0] BranchImm,
  output [5:0] BranchBits,
  output [31:0] StoreImm
);

  wire decode_black_box_1_p6, not_1_out, not_3_out, or_1_out, or_2_out, or_7_out, undriven, undriven_2;
  wire [3:0] decode_black_box_1_p7;
  wire [3:2] not_2_out;
  wire [31:0] decode_black_box_1_p8;

  or or_1 (or_1_out, ZapIF, ZapDec);
  // Decode_Black_Box decode_black_box_1: pin names not known; wires that end beside it: instr, rs1, rs2, rd, imm, decode_black_box_1_p6, decode_black_box_1_p7, decode_black_box_1_p8[0], decode_black_box_1_p8[1], decode_black_box_1_p8[2], decode_black_box_1_p8[3], decode_black_box_1_p8[4], decode_black_box_1_p8[5], decode_black_box_1_p8[6], decode_black_box_1_p8[7], decode_black_box_1_p8[8], decode_black_box_1_p8[9], decode_black_box_1_p8[10], decode_black_box_1_p8[11], decode_black_box_1_p8[12], decode_black_box_1_p8[13], decode_black_box_1_p8[14], decode_black_box_1_p8[15], decode_black_box_1_p8[16], decode_black_box_1_p8[17], decode_black_box_1_p8[18], decode_black_box_1_p8[19], ZeroOutA, AUIPC, decode_black_box_1_p8[22], decode_black_box_1_p8[23], decode_black_box_1_p8[24], decode_black_box_1_p8[25], decode_black_box_1_p8[26], decode_black_box_1_p8[27], decode_black_box_1_p8[28], decode_black_box_1_p8[29], decode_black_box_1_p8[30]
  or or_2 (or_2_out, instr[4], ~instr[5]);  // OR_Gate
  and and_1 (BranchBits[0], decode_black_box_1_p8[31], not_1_out);
  and and_2 (BranchBits[3], decode_black_box_1_p8[28], not_1_out);
  and and_3 (BranchBits[5], decode_black_box_1_p8[26], not_1_out);
  and and_4 (BranchBits[1], decode_black_box_1_p8[30], not_1_out);
  and and_5 (BranchBits[2], decode_black_box_1_p8[29], not_1_out);
  and and_6 (BranchBits[4], decode_black_box_1_p8[27], not_1_out);
  or or_3 (set, decode_black_box_1_p8[13], decode_black_box_1_p8[12], decode_black_box_1_p8[11], decode_black_box_1_p8[10]);
  not not_1 (not_1_out, or_1_out);
  or or_4 (shiftbyregval, decode_black_box_1_p8[14], decode_black_box_1_p8[16], decode_black_box_1_p8[18]);
  or or_5 (setsign, decode_black_box_1_p8[11], decode_black_box_1_p8[10]);
  not not_2 (not_2_out[2], not_2_out[3]);
  or or_6 (useImm, decode_black_box_1_p6, decode_black_box_1_p8[23]);
  Multiplexer #(.width(4), .enable("false")) multiplexer_1 (
    .in0(decode_black_box_1_p7), .in1({not_2_out, {2{not_2_out[2]}}}), .out(ALUop), .sel(not_2_out[3]));
  assign BranchImm = {{19{instr[31]}}, {instr[31], instr[7], instr[30:25], instr[11:8], instr[4]}};  // Bit_Extender bit_extender_1
  assign StoreImm = {{20{instr[31]}}, {instr[31:25], instr[11:7]}};  // Bit_Extender bit_extender_2
  and and_7 (JAL, decode_black_box_1_p8[24], not_1_out);
  and and_8 (JALR, decode_black_box_1_p8[25], not_1_out);
  or or_7 (or_7_out, or_2_out, decode_black_box_1_p8[24]);
  not not_3 (not_3_out, or_1_out);
  and and_9 (LW, decode_black_box_1_p8[22], not_1_out);
  and and_10 (LB, undriven, not_1_out);
  assign JALimm = {{11{instr[31]}}, {instr[31], instr[19:12], instr[20], instr[30:21], instr[4]}};  // Bit_Extender bit_extender_3
  or or_8 (not_2_out[3], decode_black_box_1_p8[25], decode_black_box_1_p8[22], decode_black_box_1_p8[24], undriven, decode_black_box_1_p8[23], undriven_2, decode_black_box_1_p8[31], decode_black_box_1_p8[30], decode_black_box_1_p8[29], decode_black_box_1_p8[28], decode_black_box_1_p8[27], decode_black_box_1_p8[26]);
  and and_11 (SW, decode_black_box_1_p8[23], not_1_out);
  and and_12 (regWE, or_7_out, not_3_out);
  and and_13 (SB, undriven_2, not_1_out);

  // Notes on the sheet:
  //   Feel free to output the 1 hot if you want!
endmodule

module Execute (
  input  [31:0] A,
  input  [31:0] B,
  input  [4:0] rB,
  input  [31:0] imm,
  input  useImm,
  input  [3:0] ALUop,
  input  shiftbyregval,
  input  UsePC,
  input  [31:0] PC,
  input  [31:0] BranchImm,
  input  [5:0] BranchBits,
  input  ZeroA,
  output [31:0] result,
  output Branch
);

  wire not_1_out, or_1_out;
  wire [4:0] multiplexer_4_out;
  wire [31:0] and_1_out, bit_extender_1_out, multiplexer_1_out, multiplexer_2_out, multiplexer_3_out,
       multiplexer_5_out;

  assign bit_extender_1_out = {{31{not_1_out}}, not_1_out};  // Bit_Extender bit_extender_1
  not not_1 (not_1_out, ZeroA);
  Multiplexer #(.width(32), .enable("false")) multiplexer_1 (
    .in0(imm), .in1(BranchImm), .out(multiplexer_1_out), .sel(Branch));
  Multiplexer #(.width(32), .enable("false")) multiplexer_2 (
    .in0(B), .in1(multiplexer_1_out), .out(multiplexer_2_out), .sel(useImm));
  Multiplexer #(.width(32), .enable("false")) multiplexer_3 (
    .in0(multiplexer_2_out), .in1(A), .out(multiplexer_3_out), .sel(shiftbyregval));
  Multiplexer #(.width(5), .enable("false")) multiplexer_4 (
    .in0(rB), .in1(B[4:0]), .out(multiplexer_4_out), .sel(shiftbyregval));
  BranchControl branchcontrol_1 (.A(A), .B(B), .BranchBits(BranchBits), .Branch(Branch));
  Multiplexer #(.width(32), .enable("false")) multiplexer_5 (
    .in0(A), .in1(PC), .out(multiplexer_5_out), .sel(or_1_out));
  or or_1 (or_1_out, UsePC, Branch);
  assign and_1_out = multiplexer_5_out & bit_extender_1_out;  // AND_Gate and_1, 32 bits wide
  // ALU alu_1: pin names not known; wires that end beside it: and_1_out, multiplexer_3_out, ALUop, multiplexer_4_out, result
endmodule

module MUX3to1 (
  input  [1:0] Sel,
  input  [31:0] EX,
  input  [31:0] WB,
  input  [31:0] ME,
  output [31:0] out_5
);

  wire [31:0] multiplexer_1_out;

  Multiplexer #(.width(32), .enable("false")) multiplexer_1 (.in0(EX), .in1(WB), .out(multiplexer_1_out), .sel(Sel[0]));
  Multiplexer #(.width(32), .enable("false")) multiplexer_2 (
    .in0(multiplexer_1_out), .in1(ME), .out(out_5), .sel(Sel[1]));
endmodule

module StallLogic (
  input  LW,
  input  LB,
  input  [4:0] IF_D_R1,
  input  [4:0] D_EX_RD,
  input  [4:0] IF_D_R2,
  output Stall
);

  wire and_1_out, and_2_out, or_1_out, or_2_out, xnor_1_out, xnor_2_out, xnor_3_out, xnor_4_out, xnor_5_out,
       xnor_6_out, xnor_7_out, xnor_8_out, xnor_9_out, xnor_10_out;

  or or_1 (or_1_out, LW, LB);
  xnor xnor_1 (xnor_1_out, IF_D_R1[0], D_EX_RD[0]);
  xnor xnor_2 (xnor_2_out, IF_D_R1[1], D_EX_RD[1]);
  xnor xnor_3 (xnor_3_out, IF_D_R1[2], D_EX_RD[2]);
  xnor xnor_4 (xnor_4_out, IF_D_R1[3], D_EX_RD[3]);
  xnor xnor_5 (xnor_5_out, IF_D_R1[4], D_EX_RD[4]);
  xnor xnor_6 (xnor_6_out, D_EX_RD[0], IF_D_R2[0]);
  xnor xnor_7 (xnor_7_out, D_EX_RD[1], IF_D_R2[1]);
  xnor xnor_8 (xnor_8_out, D_EX_RD[2], IF_D_R2[2]);
  xnor xnor_9 (xnor_9_out, D_EX_RD[3], IF_D_R2[3]);
  xnor xnor_10 (xnor_10_out, D_EX_RD[4], IF_D_R2[4]);
  and and_1 (and_1_out, xnor_1_out, xnor_2_out, xnor_3_out, xnor_4_out, xnor_5_out);
  and and_2 (and_2_out, xnor_6_out, xnor_7_out, xnor_8_out, xnor_9_out, xnor_10_out);
  or or_2 (or_2_out, and_1_out, and_2_out);
  and and_3 (Stall, or_1_out, or_2_out);
endmodule

module BranchControl (
  input  [31:0] A,
  input  [31:0] B,
  input  [5:0] BranchBits,
  output Branch
);

  wire and_1_out, and_2_out, and_3_out, and_4_out, comparator_black_box_1_p3, comparator_black_box_1_p4,
       comparator_black_box_1_p5, comparator_black_box_1_p6, not_1_out, or_2_out, or_3_out, or_4_out;

  // Comparator_Black_Box comparator_black_box_1: pin names not known; wires that end beside it: A, B, comparator_black_box_1_p3, comparator_black_box_1_p4, comparator_black_box_1_p5, comparator_black_box_1_p6
  or or_1 (comparator_black_box_1_p3, BranchBits[5], BranchBits[4], BranchBits[3], BranchBits[2]);
  or or_2 (or_2_out, comparator_black_box_1_p4, comparator_black_box_1_p5);
  or or_3 (or_3_out, BranchBits[2], BranchBits[0]);
  or or_4 (or_4_out, BranchBits[3], BranchBits[1]);
  and and_1 (and_1_out, or_2_out, or_3_out);
  and and_2 (and_2_out, comparator_black_box_1_p5, BranchBits[5]);
  and and_3 (and_3_out, comparator_black_box_1_p6, or_4_out);
  not not_1 (not_1_out, comparator_black_box_1_p5);
  and and_4 (and_4_out, not_1_out, BranchBits[4]);
  or or_5 (Branch, and_1_out, and_2_out, and_3_out, and_4_out);

  // Notes on the sheet:
  //   If A != B and instruction is BNE, branch
  //   If A < B and instruction is BLT or BLTU, branch
  //   If A == B and instruction is BEQ, branch
  //   if(a>b) || (a==b) and instruction is BGE or BGEU, branch
  //   BEQ
  //   BLT/BLTU
  //   BGE/BGEU
  //   BNE
endmodule
